# Fritzing sketch wiring (saved by Fritzing 0.9.4)
breadboards: 1

parts:
  U1 = NodeMCU V1.0
  NEOPIXEL1 = Neopixel Strip -- White (60/m) [part_number=1138]
  NEOPIXEL2 = Neopixel Strip -- White (60/m) [part_number=1138]
  NEOPIXEL3 = Neopixel Strip -- White (60/m) [part_number=1138]
  NEOPIXEL4 = Neopixel Strip -- White (60/m) [part_number=1138]
  J1 = Basic Servo
  J2 = Basic Servo

nets:
  N1: U1.D1, NEOPIXEL4.DI
  N2: U1.D4, J1.pulse
  GND: U1.GND, NEOPIXEL1.GND, NEOPIXEL2.GND, NEOPIXEL3.GND, NEOPIXEL4.GND, J1.gnd, J2.gnd
  N3: U1.D5, NEOPIXEL1.DI
  N4: U1.D6, NEOPIXEL2.DI
  N5: U1.D7, NEOPIXEL3.DI
  N6: U1.RX, J2.pulse
  +5V: NEOPIXEL1.+5V, NEOPIXEL2.+5V, NEOPIXEL3.+5V, NEOPIXEL4.+5V, J1.vcc, J2.vcc

notes:
  Moon LEDs (4)
  Temp Tower LEDs (7)
  Cloud LED (1)
  Sun LED (1)
  Sun / Moon Servo
  Cloud Servo

custom parts:
  NodeMCU V1.0: ESP8266 based NodeMCU
  Neopixel Strip -- White (60/m): Neopixel Strip, White, 60 pixels per meter.
